# Fritzing sketch shield (saved by Fritzing 0.9.2b)
breadboards: 1

parts:
  Part1 = Arduino Mega 2560 (Rev3)
  U2 = mystery part, 3 pins [chip_label=? spacing=300mil]  # not connected
  JP2 = Header 12 [package=1x12_machine-pin-header_lock.004]  # not connected
  Master/Slave_toggle = Toggle Switch [package=THT]

nets:
  N1: Part1.D14/TX3, Master/Slave_toggle.COM
  N2: Part1.RESET, Part1.D30
  N3: Part1.5V, Master/Slave_toggle.L2
  N4: Part1.GND, Master/Slave_toggle.L1

// code stored in the sketch: V0.8build116shield.ino
//Digital Pins
#define FF1pin            41 //fault flag 1
#define FF2pin            39 //fault flag 2
#define motorResetPin     49 //motor driver reset pin
#define pwmHPin           46 //motor driver PWM high pin
#define pwmLPin           44 //motor driver PWM low pin
#define dirPin            43 //motor driver direction pin
#define MagnetSensorPin   19 //pin to magnet hall sensor


//Analog Pins
#define PSpin             A12 //motor driver power supply pin
#define CSPin             A13 //motor driver current sensor pin
#define RANDOM_NOISE_PIN  A3
//#define potPin            A2 //potentiometer pin (optional)

//LEDS
#define LED1        35
#define LED2        37    

//State machine
#define numOfStates         8
#define ZERO_STATE          0x01
#define WAIT_FOR_RESPONSE   0x02
#define PULL_STATE          0x03
#define PULL_AND_COUNT      0x04      
#define PULL_SLOW           0x05

//System modes
#define MS_IDLE         0xAA
#define MS_RUNNING      0xAB
#define MS_CALIBRATION  0xAC
#define SL_IDLE         0xBA
#define SL_RUNNING      0xBB
#define SL_CALIBRATION  0xBC

//PID
#define Kp                0.014036
#define Ki                0.95046
#define Kd                0.0

//Other Constants
#define pi                      3.14159
#define radius                  6.5 //[cm] radius of the wheel. represents velocity at the end point
#define ropeRadius              2.23 // [cm] represent velocity where the rope is
#define numOfMagnets            2 //number of magnets available on the motor
#define maximumMotorVelocity    25 //maximum motor velocity 157.08[rad/second] = 2*pi*1500[RPM]/60[seconds] or 3.5[m/s]=2*pi*roperadius(0.223[m])*1500[RPM]/60[sec] or 1500/60 = 25 [RPS]
#define VMEASURE_SAMPLE_TIME    500 //what is the timeframe for velocity measurement. [ms]
#define SLOW_VELOCITY           0.6 //the motor use this velocity when moveing slowly from one side to the other. [m/second]
#define MAX_PWM_VALUE           255
#define NOMINAL_TRACK_LENGTH    2500 //nominal length of the track (distance between motors) [cm]
#define SAFETY_DISTANCE         10 //safety distance from the edges in numOfmagnets
#define DELAY_BETWEEN_RUNNINGS  2000 //time to wait between runnings in [ms]
#define MAXIMUM_REQUESTED_VELOCITY 3.5 //the maximum velocity that can be requested on the webpage

//XBEE
#define XBEE_DATA_RATE 9600

//XBEE messages
#define START_BYTE          0xC8
#define STOP_BYTE           0xD6
#define CLEAR_BUFFER        0xDD

//Master->slave
#define GOTO_CALIBRATION    0x6B
#define GOTO_RUN            0x61
#define GOTO_IDLE           0x62
#define SWITCH_TO_COAST     0x63
#define KEEP_ALIVE          0x64
#define LTR_VELOCITY_UPDATE 0x65
#define LTR_DELAY_UPDATE    0x66
#define PULL_SLOWLY         0x67
#define STOP_MOTOR          0x68
#define START_PULLING       0x69
#define TRACK_LENGTH_UPDATE 0x6A

//Slave->master
#define ACK_CALIB           0x70
#define ACK_RUN             0x71
#define ACK_IDLE            0x72
#define ACK_COAST           0x73
#define DONE_PULLING        0x74
#define ACK_KA              0x75
#define ACK_VEL             0x76
#define ACK_PULL            0x77
#define ACK_STOP            0x78
#define ACK_DELAY           0x79
#define ACK_TRACK           0x7A

//HTTP messages parsing cases:
#define UPDATE_VELOCITY_RTL       0x50
#define UPDATE_VELOCITY_LTR       0x51
#define UPDATE_BEGIN_CALIBRATION  0x52
#define UPDATE_BEGIN_RUNNING      0x53
#define UPDATE_STOP               0x54
#define UPDATE_STATUS             0x55
#define UPDATE_DELAY_RTL          0x5B
#define UPDATE_DELAY_LTR          0x5C
#define OPEN_FILE 			       	  0x56

//WhatToSend states - these flags set the message that will be sent next on idle mode
#define SEND_KA                   0xF1
#define SEND_DELAY                0xF2
#define SEND_VELOCITY             0xF3

//HTTP message strings
#define MSG_RTL_VEL         "RTL_vel="
#define MSG_LTR_VEL         "LTR_vel="
#define MSG_RTL_DELAY       "RTL_delay="
#define MSG_LTR_DELAY       "LTR_delay="
#define MSG_CAL             "BeginCalibration"
#define MSG_RUN             "BeginRunning"
#define MSG_STOP            "Stop"
#define MSG_STATUS          "status"

//Ethernet
#define REQ_BUF_SZ            60 // size of buffer used to capture HTTP requests
#define WEBSITE_FILENAME      "targuino.htm" //name of the main html file on the SD card
#define JAVASCRIPT_FILENAME   "targuino.js" //javascript filename
#define JS_UISLIDER_FILENAME  "nuslider.js"
#define CSS_UISLIDER_FILENAME "nuslider.css"
#define JQUERY_FILENAME       "jquery.js"
#define CSS_FILENAME          "targuino.css" //css filename
#define JPG_FILENAME          "targuino.jpg" //jpg filename
#define XML_FILENAME          "targuino.xml"
#define ICO_FILENAME          "favicon.png"

//Watchdogs and timers
#define DELAY_BETWEEN_KA          3000 //time between keep-alive messages
#define KA_WATCHDOG               3 //maximum keepalive messages to wait for SL response before error message appears
#define MAXIMUM_NUM_OF_RESENDS    3 //timeout for a response from the other side
#define RESEND_TIMOUT             5000 //timout to resend message
#define FINITE_WAITING_TIMEOUT    40000 //finite timeout. after this time the system goes back to idle

//Motor State description variables
boolean DIR                         = 0; // 1 - clockwise, 0 - counter-clockwise
volatile unsigned int Revolutions   = 0; //number of revolutions. global variable needs to be defined as volatile in order to be used by interrupts
volatile unsigned int RunLength     = 0; //this variable counts revolutions during a run and compare it to lTrack [Revolutions]. It also delivers the length to lTrack during calibration
unsigned int lTrack                 = 0; //stores the length of the track (= distance between motors). needs to be written to the EEPROM in the future
float vAngular                      = 0;
float vLinear                       = 0;
float K                             = 0.5; //averaging constant between very different velocity measurements
float kk                            = 0;
int distance_from_edge              = 0; //this variable contains the calculated distance from the opposite edge 

//Timer and watchdog variables
unsigned long PreviousInterruptTime       = 0;
unsigned long CurrentTime                 = 0;
unsigned int deltaT                       = 0;
unsigned int tBeginMovement               = 0; 
unsigned int timeGuard                    = 0;
unsigned int maximumRunTime               = 0; //this is them maximum time the motor can run before watchdog is up
unsigned long PrevMsgSent                 = 0; //stores the last time KEEP-ALIVE msg was sent
int numOfKAmsgs                           = 0; //stores the number of keealive msgs that were sent
int numOfresends                          = 0; //stores the number of times a message was resent
int numOfCycUnknown                       = 0; //stores the number of times slave got unknown messages
int nDroppedMsgs                          = 0;
unsigned long PreviousTimeForGeneralTasks = 0; //this is a timer in loop() for general tasks
boolean hasStopBeenClickedOnce            = false;

/* PID Variables*/
double measuredIn = 0; //[m/s]measured velocity
double desiredIn  = 0; // this variable stores the desired velocity in PWM range (0-255)
double sysIn      = 0; //the calculated input to the driver
PID myPID(&measuredIn, &sysIn, &desiredIn, Kp, Ki, Kd, DIRECT);

//system state variables
boolean MS              = 0; //is arduino in Master or Slave mode (0 for slave mode, 1 for master)
byte FSM_State          = ZERO_STATE; //system's currect state in the state machine. default value is ZERO_STATE - initial state (see #define)
byte sysMode            = 0; //this byte indicate two thing: 1) is this motor MS/SL   2) is the system in idle, calibration or run mode
float velLTR            = 0.0; //the velocity the user has requested for the run from left to right
float velRTL            = 0.0; //the velocity the user has requested for the run from right to left
String TarMsg           = " "; //string that contains system status
boolean stopSignal      = false; //a general flag which uses to control whether the system goes to the next stage
int LTR_delay           = 0; //delay before slave starts to pull. in [sec]
int RTL_delay           = 0; //delay before master starts to pull. in [sec]
boolean delayHasPassed  = false; //a flag states whether the delay time has passed
boolean isCloseToEdge   = false;

//Ethernet
byte mac[] 										    	   = {0xDE, 0xAD, 0xBE, 0xEF, 0xFE, 0xED};
IPAddress 				 				  			       ip(192, 168, 0, 177);
EthernetServer   			  				   			   server(80);
char HTTP_req[REQ_BUF_SZ] 						    	   = {0};  	// 0 = null in ascii
char req_index   			 			  			       = 0;       // index into HTTP_req buffer
typedef struct parsedResult {byte msgType; float value; String fileToOpen; char httpResponse;} parsedResult;

//XBEE variables
byte msgToSend[10]              = {START_BYTE, 0, 0, 0, 0, 0, 0, 0, 0, STOP_BYTE};
byte recBuff[7]                = {0, 0, 0, 0, 0, 0, 0};
byte previousTxMsg              = 0xFF; 
byte previousRxMsg             = 0;
String XBEEstatusMsg           = " ";
byte MsgCounter                = 0; //counter to be added to the messages
byte msgIndex                  = 0;
boolean isSlaveConnected       = 0;
byte whatToSend                = 0xF1;   // a flag states what should the master send to the slave: KA, delay or velocity
byte inMsgCount                = 0;
byte MsgCounterAtDest          = 0; //stores MsgCounter as it is on the other side 
byte tempByte                  = 0;
boolean isMsg                  = false;
byte msgIndDiff                = 0; //distance between message indices

//SD card
File TServerFile;
File xmlFile;

//Other variables - delete if unnecessary
int faultflag           = 0; //0- OK, 1-short, 2-overheat, 3-undervoltage
int sensorValue         = 0;
float current           = 0;
float CS                = 0;
boolean OneTimeFlag   = true;
int tempAcc             = 0;

//=====================SETUP=============================================
void setup(){
  // disable Ethernet chip
  pinMode(10, OUTPUT);
  digitalWrite(10, HIGH);
  
  //initialize XBEE
  Serial.begin(             XBEE_DATA_RATE); 
  Serial2.begin(             XBEE_DATA_RATE); //for debug purposesuffer

  Serial2.print("Targuino version 0.8 build "); Serial2.println(BUILD_NUMBER);
  
  cleanXBEE();

  //initialize digital pins. Analog pins don't require initialize
  pinMode(pwmHPin,          OUTPUT); 
  pinMode(pwmLPin,          OUTPUT);
  pinMode(dirPin,           OUTPUT); 
  pinMode(FF1pin,           INPUT); 
  pinMode(FF2pin,           INPUT); 
  pinMode(motorResetPin,    INPUT); 
  pinMode(MagnetSensorPin,  INPUT);
  pinMode(resetPin,         OUTPUT);
  pinMode(MSpin,            INPUT);

  //init leds
  pinMode(LED1, OUTPUT);
  pinMode(LED2, OUTPUT);
 
  //initialize reset pin
  digitalWrite(resetPin,           HIGH); //switching to LOW will reset the arduino

  Serial2.println("Pins initialized");

  //CHECK MASTER/SLAVE MODE
  if(digitalRead(MSpin) ==  HIGH){  
    MS = 1;
    Serial2.println("This is the master motor");
    
    //initialize default velocities and delays
    velLTR = 0; // [m/s] , default values
    LTR_delay = 0; // [m/s]
    velRTL = 0;
    RTL_delay = 0;

    sysMode = MS_IDLE;  
    //initialize Ethernet server
    Ethernet.begin(mac, ip);
    server.begin();
    initSD();
  }
  else {
    sysMode = SL_IDLE;
    Serial2.println("This is the slave motor");
  }
  
  myPID.SetOutputLimits(0,250);  //tell the PID to range between 0 and 255 (PWM range)    // some arbitrary value I've decided of. 255 is too much?
  myPID.SetMode(    AUTOMATIC); //turn the PID on
  myPID.SetSampleTime(  VMEASURE_SAMPLE_TIME);

  maximumRunTime = float(NOMINAL_TRACK_LENGTH / SLOW_VELOCITY) * 1000;
  
  Serial2.print("Maximum runtime is [ms]: "); Serial2.println(maximumRunTime);

  //setup interrupt for the magnet sensor
  attachInterrupt(4,IncrRevolution,RISING); //interrupt 4 is for pin number 19 - magnet sensor input

  PreviousInterruptTime = millis(); //start timer

  randomSeed(analogRead(RANDOM_NOISE_PIN));

}

//=====================MAIN=============================================
void loop(){
  switch (FSM_State) {
   case ZERO_STATE:
    if(OneTimeFlag){
      Serial2.println("i'm in state: zero! waiting for instructions");
      TarMsg =  "System in idle mode. Waiting for instructions <br />";
      OneTimeFlag = false;
    }
    switch(sysMode){
      case MS_IDLE:
        if(CurrentTime - PrevMsgSent > DELAY_BETWEEN_KA){
          PrevMsgSent = CurrentTime;
          switch(whatToSend){
            case SEND_KA:
              sendXBEEmsg(KEEP_ALIVE);
              whatToSend = SEND_VELOCITY;
              break;
            case SEND_VELOCITY:
              sendXBEEmsg(LTR_VELOCITY_UPDATE);
              whatToSend = SEND_DELAY;
              break;
            case SEND_DELAY:
              sendXBEEmsg(LTR_DELAY_UPDATE);
              whatToSend = SEND_KA;
              break;
          }
        numOfKAmsgs++;    //this number is zeroed if we get KA-ACK (this is handled in Serial Event)
        }

        if(numOfKAmsgs > KA_WATCHDOG){ 
          Serial2.print(float(CurrentTime / 1000)); Serial2.println(" ERROR - XBEE Slave error: no response from slave");
          XBEEstatusMsg = "No connection";
          numOfKAmsgs = 0;
          }

        break;

      case SL_IDLE:
        //resets XBEE receiving pipeline in case too many unknown messages
        if(numOfCycUnknown > 20){
          cleanXBEE();
          numOfCycUnknown = 0;
        }
        break;

      case SL_CALIBRATION:
        sendXBEEmsg(ACK_CALIB);
        Serial2.println("ACK_CAL msg sent. waiting for response...");
        setWaitForRespondMode();
        break;
      
      case MS_RUNNING:
        if(areVelocitiesLegal()){
          TarMsg =  "illigal values! Check velocity (velocity cannot be under 0.1). Aborting... <br />";
          sysMode = MS_IDLE;
          break;    
        }
        Serial2.println("GO_TO_RUN msg sent. waiting for response...");
        sendXBEEmsg(GOTO_RUN);
        setWaitForRespondMode();
        break;
      
      case SL_RUNNING:
        sendXBEEmsg(ACK_RUN);
        Serial2.println("ACK_RUN msg sent. waiting for instructions...");
        break;

      default:
        break; //do nothing
    }
    break;
   
   case WAIT_FOR_RESPONSE:
    //In case of response Serial Event would update FSM_STATE we'll move on. We're having a watchdog just in case

    if(CurrentTime - PrevMsgSent > RESEND_TIMOUT && previousTxMsg != ACK_COAST && numOfresends < 3){
      sendXBEEmsg(previousTxMsg);
      numOfresends++;
      PrevMsgSent = CurrentTime;
    }
    
    if(numOfresends > FINITE_WAITING_TIMEOUT){ //this is after 3 resends, so in total the timout is 30 seconds
      Serial2.println("wait for response: response-timout");
      coastMotor();
      FSM_State = ZERO_STATE;
      OneTimeFlag = true;
      if(MS){ 
        sysMode = MS_IDLE;
        sendXBEEmsg(STOP_MOTOR);
      }
      else{ sysMode = SL_IDLE;}
    }

    break;

   case PULL_AND_COUNT:
    
    TarMsg =  "Measuring track length. Click Stop when target is near the edge <br />";
    timeGuard = CurrentTime - tBeginMovement;

    if(OneTimeFlag){
      RunLength = 0;
      stopSignal = false;
      OneTimeFlag = false;
    }  

    if(timeGuard > maximumRunTime || stopSignal){ // target probably arrived to the other edge of the rope 
      coastMotor();
      TarMsg =  "Saving track length. To change track length repeat calibration process <br />";
      Serial2.print("saving data! length of track is: "); Serial2.print(RunLength / numOfMagnets); Serial2.println(" revolutions. Saving...");
      lTrack = RunLength; //save lTrack. In the future - maybe save to EEPROM
      sendXBEEmsg(TRACK_LENGTH_UPDATE);
      setWaitForRespondMode();
      stopSignal = false; //reset stopSignal for the future
      delayHasPassed = false;
      break;
    }
    
    if(checkTime(VMEASURE_SAMPLE_TIME)){  
      MeasureVelocityInPWM(deltaT);
      myPID.Compute();
      movemotor(DIR,sysIn,MAX_PWM_VALUE);
      Serial2.print("desiredIn = "); Serial2.print(desiredIn); Serial2.print(" measuredIn = "); Serial2.print(measuredIn); Serial2.print(" sysIn = "); Serial2.print(sysIn); Serial2.print(" RunLength = "); Serial2.println(RunLength);

     }
    break;


   case PULL_SLOW:
    
    if(MS){ TarMsg = "Starting to pull slowly. Click Stop when target is near the edge ?<br />"; }

    //Serial2.println(TarMsg);

    if(stopSignal){ //if target arrived to the other side 
      coastMotor();
      sendXBEEmsg(DONE_PULLING);
      setWaitForRespondMode();
      stopSignal = false; //reset stopSignal for future runs
      RunLength = 0;
      break;
    }


    if(checkTime(VMEASURE_SAMPLE_TIME)){  
      MeasureVelocityInPWM(deltaT);
      myPID.Compute();

      /////////////////////////////////ONLY IF THERE IS NO SENSOR! 
      if(!MS){ sysIn = desiredIn;}
      /////////////////////////////////ONLY IF THERE IS NO SENSOR!
      
      movemotor(DIR,sysIn,MAX_PWM_VALUE);
      Serial2.print("desiredIn = "); Serial2.print(desiredIn); Serial2.print(" measuredIn = "); Serial2.print(measuredIn); Serial2.print(" sysIn = "); Serial2.print(sysIn); Serial2.print("RunLength = "); Serial2.println(RunLength);
     }

    break;


   case PULL_STATE:
    
    if(OneTimeFlag){
      RunLength = 0;
      stopSignal = false;
      OneTimeFlag = false;
      if(MS){ TarMsg = "Running from side to side. Click stop to abort <br />"; }
    }    

    timeGuard = CurrentTime - tBeginMovement;  
    distance_from_edge = lTrack - RunLength;

    //implement time delay
    if(MS && timeGuard > RTL_delay * 1000 && !delayHasPassed){ //if RTL_Delay has passed (for master) - raise the flag to start pulling
      Serial2.println("Delay passed");
      delayHasPassed = true;
    }  
    else if(!MS && timeGuard > LTR_delay * 1000 && !delayHasPassed){ //if LTR_Delay has passed (for slave) - raise the flag to start pulling
      Serial2.println("Delay passed");
      delayHasPassed = true; 
    }    

    if(distance_from_edge < (2 * SAFETY_DISTANCE) && !isCloseToEdge){
      desiredIn = 0.7 * desiredIn; //reducing velocity towards the edge
      isCloseToEdge = true;
     }

    if(distance_from_edge < SAFETY_DISTANCE || stopSignal){ //if target arrived to the other side 
      Serial2.print("Near the edge! Distance is now: "); Serial2.print(distance_from_edge); Serial2.println(" revolutions. stopping...");
      coastMotor();
      
      if(MS){ 
        sendXBEEmsg(START_PULLING);
        Serial2.println("Coasting. slave motor should be pulling now. waiting for donePulling");
      }
      else { 
        sendXBEEmsg(DONE_PULLING);
        Serial2.println("Coasting. slave: donePulling");
      }
      setWaitForRespondMode();
      stopSignal = false; //reset stopSignal for future runs
      delayHasPassed = false; //reset delayhaspassed for future runs
      RunLength = 0;
      isCloseToEdge = false;
      Serial2.print("distance_from_edge: "); Serial2.println(distance_from_edge);
      break;
    }

    if(delayHasPassed && checkTime(VMEASURE_SAMPLE_TIME)){  
      MeasureVelocityInPWM(deltaT);
      myPID.Compute();
      /////////////////////////////////ONLY IF THERE IS NO SENSOR!
      if(!MS){ 
        sysIn = desiredIn;
      }
      /////////////////////////////////ONLY IF THERE IS NO SENSOR!
      movemotor(DIR,sysIn,MAX_PWM_VALUE);
     }

     if(delayHasPassed && timeGuard > 1000){
      Serial2.print("DHP: "); Serial2.print(delayHasPassed); Serial2.print(" timeGuard:"); Serial2.print(timeGuard); Serial2.print(" Distance:"); Serial2.print(distance_from_edge); Serial2.print(" sysIn = "); Serial2.print(sysIn); Serial2.print(" DesiredIn"); Serial2.println(desiredIn);      
      tBeginMovement = CurrentTime;
      /////////////////////////////////ONLY IF THERE IS NO SENSOR!
      if(!MS){ 
        distance_from_edge = distance_from_edge - 1;
      }
      /////////////////////////////////ONLY IF THERE IS NO SENSOR!
     }
    break;
       
   default:
    coastMotor(); //just in case something happens...
    Serial2.print("Got into default mode. FSM_state = "); Serial2.println(FSM_State);
    FSM_State = ZERO_STATE;
    OneTimeFlag = true;
    break;
	} 
  
  //Ethernet communication handling
  if(MS){
    EthernetClient client = server.available();  // try to get client
    if(client){
    	//Serial2.println("client found!");
      boolean currentLineIsBlank = true;
  	  while(client.connected()){ 
        if(client.available()){   // client data available to read
			    char c = client.read(); // read 1 byte (character) from client
          //Serial2.print(c);
          //this if and elseif are due to (apparent) lack of memory. REQ_BUF_SZ > 100 causes arduino to reset. So we decided to take only the first 80 bytes
           if(req_index < REQ_BUF_SZ - 1){  /* limit the size of the stored received HTTP request.  buffer first part of HTTP request in HTTP_req. leave last element in array as 0 to null terminate string (REQ_BUF_SZ - 1)*/
              HTTP_req[req_index] = c;          // save HTTP request character
              req_index++;
          	}
          // last line of client request is blank and ends with \n
          // respond to client only after last line received
          if (c == '\n' && currentLineIsBlank) {
              
              parsedResult out = parseHTTPmsg(HTTP_req);

              switch(out.msgType){
                case UPDATE_VELOCITY_RTL:
                  velRTL = out.value;
                  Serial2.print("RTL velocity has been updated to: "); Serial2.println(velRTL);
                  break;

                case UPDATE_VELOCITY_LTR:
                  velLTR = out.value;
                  Serial2.print("LTR velocity has been updated to: "); Serial2.println(velLTR);
                  whatToSend = SEND_VELOCITY;
                  break;

                case UPDATE_BEGIN_CALIBRATION:
                  if(!isSlaveConnected){
                    TarMsg =  "Calibration sequence has not commenced - no connection to slave <br />";
                    Serial2.println(TarMsg);
                    break;
                  }
                  Serial2.print(float(CurrentTime / 1000)); Serial2.println(" BeginCalibration has been received");
                  sysMode = MS_CALIBRATION;
                  sendXBEEmsg(GOTO_CALIBRATION);
                  setWaitForRespondMode();
                  break;

                case UPDATE_BEGIN_RUNNING:
                  if(!isSlaveConnected){
                    TarMsg =  "Running sequence has not commenced - no connection to slave <br />";
                    Serial2.println(TarMsg);
                    break;
                  }
                  sysMode = MS_RUNNING;
                  Serial2.print(float(CurrentTime / 1000)); Serial2.println(" BeginRunning has been received");
                  break;

                case UPDATE_STOP:
                  if(FSM_State == WAIT_FOR_RESPONSE){
                    sendXBEEmsg(STOP_MOTOR);
                    Serial2.print(float(CurrentTime / 1000)); Serial2.println("Stop msg while waiting!");
                    break;
                  }
                  else if(FSM_State == PULL_SLOW || FSM_State == PULL_AND_COUNT || FSM_State == PULL_STATE){
                    Serial2.print(float(CurrentTime / 1000)); Serial2.println("Stop msg while pullSlow / PullAndCount / PullState!");
                    stopSignal = true; 
                  }

                  if(hasStopBeenClickedOnce){
                    coastMotor();
                    sendXBEEmsg(STOP_MOTOR);
                    Serial2.print(float(CurrentTime / 1000)); Serial2.println("General stop msg! two stop presses were detected");
                    setWaitForRespondMode();
                    hasStopBeenClickedOnce = false;
                    break;
                  }

                  hasStopBeenClickedOnce = true; //to determine whether we clicked stop once or twice
                  break;

                case UPDATE_STATUS:
                  //Serial2.println("status update");
                  sendHTTPResponse('x',client);
                  printXML(client);
                  break;
                
                case OPEN_FILE:
                  Serial2.print(float(CurrentTime / 1000)); Serial2.print(" Sending requested file..."); Serial2.println(out.fileToOpen);
                  sendHTTPResponse(out.httpResponse, client);
                  sendFile(out.fileToOpen, client);
                  break;

                case UPDATE_DELAY_RTL:
                  RTL_delay = out.value;
                  Serial2.print("RTL delay has been updated to: "); Serial2.println(RTL_delay);
                  break;

                case UPDATE_DELAY_LTR:
                  LTR_delay = out.value;
                  Serial2.print("LTR delay has been updated to: "); Serial2.println(LTR_delay);
                  whatToSend = SEND_DELAY;
                  break;

                default:
                  break;

              }

              req_index = 0;// reset buffer index and all buffer elements to 0
              StrClear(HTTP_req, REQ_BUF_SZ);
              break;
            }

            // every line of text received from the client ends with \r\n
            if (c == '\n'){ 		currentLineIsBlank = true; } // last character on line of received text, starting new line with next character read
            else if (c != '\r'){   currentLineIsBlank = false; }// a text character was received from client
        } // end if (client.available())
      } // end while (client.connected())
      delay(300);      // give the web browser time to receive the data
      client.stop(); // close the connection	
      //Serial2.println("Connection closed");
  	} //end if(client)
  }

  
  //Do some general tasks
  CurrentTime = millis(); //main timer for all system purposes
  
  if(CurrentTime - PreviousTimeForGeneralTasks > 5000){ 
    //A. zeroize hasStopBeenClickedOnce after 5 seconds - resets two stop presses
    hasStopBeenClickedOnce = false;
    PreviousTimeForGeneralTasks = CurrentTime;

    //B. display some debug data on serial2
    if(FSM_State == ZERO_STATE){
      Serial2.print(float(CurrentTime / 1000)); Serial2.print(" State: "); Serial2.print(FSM_State, HEX); Serial2.print(" Mode: "); Serial2.print(sysMode,HEX); 
          
      if(MS){   Serial2.print(" RTL_delay: "); Serial2.print(RTL_delay); Serial2.print(" RTL_Vel: "); Serial2.print(velRTL); }
      else{     Serial2.print(" LTR_delay: "); Serial2.print(LTR_delay); Serial2.print(" LTR_Vel: "); Serial2.print(velLTR); }

      Serial2.print(" lTrack: "); Serial2.println(lTrack);

      Serial2.print(float(CurrentTime / 1000)); Serial2.print(" OutMsgIndex: "); Serial2.print(MsgCounter); Serial2.print(" InMsgIndexFromOtherSide: "); Serial2.println(MsgCounterAtDest);        
    }

  }

  //current sensor
  sensorValue = analogRead(CSPin);  
  current = ( map(sensorValue, 0, 1023, 0, 5) - 2.5) / 0.066;


if(Serial.available() > 0){
  SerialProcess();
}

}//end loop
  
//=====================FUNCTIONS=============================================

void SerialProcess(){
  
  byte processedMSG = 0xFE; //default "empty" value
  tempByte = Serial.read();
  //Serial2.print(float(CurrentTime / 1000)); Serial2.print(" buffer size: "); Serial2.print(Serial.available()); Serial2.print(" bytes. "); Serial2.print("tempByte: "); Serial2.println(tempByte,HEX);
    
  if(tempByte == STOP_BYTE || msgIndex > 7){ //maximum value of msgIndex is 4 (last index of recBuff) 
    isMsg = false;
    msgIndex = 0;
    processedMSG = procRecMsg();
    inMsgCount = recBuff[3];
  }
  else if(isMsg){
    recBuff[msgIndex] = tempByte;
    //Serial2.print("recBuff["); Serial2.print(msgIndex); Serial2.print("]="); Serial2.println(recBuff[msgIndex],HEX);
    msgIndex++;
    return;
  }
  else if(tempByte == START_BYTE){ 
    clrXBEErecBuff(); //clear recieve buffer before starting a new recieving process
    isMsg = true;
    return;
  }
  else{ 
    return;
  }

  if(processedMSG == previousRxMsg){ //drop double messages
      Serial2.print(float(CurrentTime / 1000)); Serial2.print(" Message number "); Serial2.print(inMsgCount); Serial2.print(" dropped: "); Serial2.println(processedMSG, HEX);
      nDroppedMsgs++;
      numOfKAmsgs = 0;
      return;
      } 
  else if(processedMSG != previousRxMsg){
     previousRxMsg = processedMSG; 
     Serial2.print(float(CurrentTime / 1000)); Serial2.print(" Proccessed msg: "); Serial2.print(processedMSG,HEX); Serial2.print(" timestamp: "); Serial2.print(recBuff[3]); Serial2.print(" value: "); Serial2.println(recBuff[4]);
    }

  switch(processedMSG){
    case ACK_KA: //keep alive ack
      numOfKAmsgs = 0;
      XBEEstatusMsg = "Live!";
      isSlaveConnected = true;
      MsgCounterAtDest = recBuff[4];
      Serial2.print(float(CurrentTime / 1000)); Serial2.print(" Keep alive ack, msg index is "); Serial2.println(inMsgCount);
      if( abs(MsgCounter - MsgCounterAtDest) % 255 > 3 && MsgCounter > 3){
        msgIndDiff = abs(MsgCounter - MsgCounterAtDest) % 255;
        sendXBEEmsg(CLEAR_BUFFER);
        Serial2.print(float(CurrentTime / 1000)); Serial2.println(" clear buffer request sent");
      }
      break;

    case ACK_VEL:
      numOfKAmsgs = 0;
      XBEEstatusMsg = "Live!";
      isSlaveConnected = true;
      //Serial2.print(float(CurrentTime / 1000)); Serial2.println(" LTR velocity ack received");
      break;

    case ACK_DELAY:
      numOfKAmsgs = 0;
      XBEEstatusMsg = "Live!";
      isSlaveConnected = true;
      //Serial2.print(float(CurrentTime / 1000)); Serial2.println(" LTR delay ack received");
      break;

    case GOTO_CALIBRATION:
      sysMode = SL_CALIBRATION;
      sendXBEEmsg(ACK_CALIB);
      setWaitForRespondMode();
      Serial2.print(float(CurrentTime / 1000)); Serial2.print(" slave: gotocalibration msg received. sent: "); Serial2.println(ACK_CALIB,HEX);
      break;

    case GOTO_RUN:
      sysMode = SL_RUNNING;
      sendXBEEmsg(ACK_RUN);
      setWaitForRespondMode();
      Serial2.print(float(CurrentTime / 1000)); Serial2.println(" goto run received");  
      break;

    case GOTO_IDLE:
      sysMode = SL_IDLE;
      FSM_State = ZERO_STATE;
      OneTimeFlag = true;
      sendXBEEmsg(ACK_IDLE);
      Serial2.print(float(CurrentTime / 1000)); Serial2.println(" goto idle received");  
      break;

    case SWITCH_TO_COAST:
      coastMotor();
      sendXBEEmsg(ACK_COAST);
      setWaitForRespondMode();
      Serial2.print(float(CurrentTime / 1000)); Serial2.println(" switching to coast...");  
      break;

    case KEEP_ALIVE:
      MsgCounterAtDest = recBuff[4];
      Serial2.print(float(CurrentTime / 1000)); Serial2.print(" Keep alive received, msg index is "); Serial2.println(inMsgCount);
      if( abs(MsgCounter - MsgCounterAtDest) % 255 > 3 && MsgCounter > 3){
        msgIndDiff = abs(MsgCounter - MsgCounterAtDest) % 255;
        sendXBEEmsg(CLEAR_BUFFER);
        Serial2.println("clear buffer request sent");
      }
      else{
        sendXBEEmsg(ACK_KA);
      } 
      break;

    case ACK_CALIB:
      coastMotor();
      sendXBEEmsg(PULL_SLOWLY);
      setWaitForRespondMode();
      Serial2.print(float(CurrentTime / 1000)); Serial2.println(" ack calib received. sent PullSlowly msg"); 
      break;

    case ACK_RUN:
      coastMotor();
      sendXBEEmsg(PULL_SLOWLY);
      setWaitForRespondMode();
      Serial2.print(float(CurrentTime / 1000)); Serial2.println(" ack run received, waiting for donePulling msg"); 
      break;

    case ACK_IDLE:
      sysMode = MS_IDLE;
      FSM_State = ZERO_STATE;
      OneTimeFlag = true;
      Serial2.print(float(CurrentTime / 1000)); Serial2.println(" ack idle received, going back to idle"); 
      break;

    case ACK_TRACK:
          sendXBEEmsg(GOTO_IDLE); 
          setWaitForRespondMode();
          Serial2.print(float(CurrentTime / 1000)); Serial2.println(" track length recieved on slave side"); 
          break;

    case ACK_COAST: //only master motor get ack_coast
      switch(sysMode){
        case MS_CALIBRATION:
          desiredIn = (double) convertMagnetsToPWM(convertVelToMagnets(SLOW_VELOCITY), VMEASURE_SAMPLE_TIME);
          FSM_State = PULL_AND_COUNT;
          OneTimeFlag = true;
          tBeginMovement = CurrentTime;
          Serial2.print(float(CurrentTime / 1000)); Serial2.println(" ack coast received in master calibration mode"); 
          break;
        case MS_RUNNING:
          desiredIn = (double) convertMagnetsToPWM(convertVelToMagnets(velRTL), VMEASURE_SAMPLE_TIME);
          FSM_State = PULL_STATE;
          OneTimeFlag = true;
          tBeginMovement = CurrentTime;
          Serial2.println("ack coast received in master running mode"); 
          break;
        default:
          Serial2.println("ERROR - ACK_COAST receievd but I don't know what to do with it");
          break; //do nothing
      }
      break;

    case DONE_PULLING:
      sendXBEEmsg(SWITCH_TO_COAST);
      setWaitForRespondMode();
      Serial2.println("done pulling received, waiting for ack_coast"); 
      break;  
      
    case PULL_SLOWLY:
      sendXBEEmsg(ACK_PULL);
      desiredIn = (double) convertMagnetsToPWM(convertVelToMagnets(SLOW_VELOCITY), VMEASURE_SAMPLE_TIME);
      FSM_State = PULL_SLOW;
      tBeginMovement = CurrentTime;
      Serial2.print("starting to pull at: "); Serial2.println(desiredIn);
      break;

    case STOP_MOTOR:
      if(FSM_State == PULL_SLOW){
        stopSignal = true;
        break;
      }
      else if(FSM_State == PULL_STATE){
        coastMotor();
        FSM_State = ZERO_STATE;
        OneTimeFlag = true;
        sendXBEEmsg(ACK_STOP);
        sysMode = SL_IDLE; //only slave can get this message
        break;
      } 
      else if(sysMode == SL_RUNNING && FSM_State == WAIT_FOR_RESPONSE){
        coastMotor();
        FSM_State = ZERO_STATE;
        OneTimeFlag = true;
        sendXBEEmsg(ACK_STOP);
        sysMode = SL_IDLE; //only slave can get this message
        break;
      }
      break;

    case ACK_STOP:
      if(FSM_State == WAIT_FOR_RESPONSE){
        Serial2.println("Ack_stop recieved while in Wait_for_response");
        FSM_State = ZERO_STATE;
        OneTimeFlag = true;
        sysMode = MS_IDLE;
      }
      break;

    case ACK_PULL:
      setWaitForRespondMode();
      break;

    case START_PULLING:
      if(sysMode != SL_RUNNING){
        Serial2.println("StartPulling error - sysMode is not in SL__RUNNING mode");
        break;
      }
      else{
        desiredIn = (double) convertMagnetsToPWM(convertVelToMagnets(velLTR), VMEASURE_SAMPLE_TIME);
        FSM_State = PULL_STATE;
        tBeginMovement = CurrentTime;
        Serial2.println("Going into Pull_state / SL");
        break;
      }

    case 0xFF:
      // message totally corrupted
      break;

    case CLEAR_BUFFER:
      cleanXBEE();
      break;

    case LTR_VELOCITY_UPDATE:
      velLTR = ( (float) (int) recBuff[4] ) / 10;
      //Serial2.print(float(CurrentTime / 1000)); Serial2.print(" LTR vel received: "); Serial2.println(velLTR);
      sendXBEEmsg(ACK_VEL);
      break;
    
    case LTR_DELAY_UPDATE:
      LTR_delay = (int) recBuff[4];
      //Serial2.print(float(CurrentTime / 1000)); Serial2.print(" LTR delay received: "); Serial2.println(LTR_delay); 
      sendXBEEmsg(ACK_DELAY);
      break;

    case TRACK_LENGTH_UPDATE:
      lTrack = (int) recBuff[4] * 255 + (int) recBuff[5];
      Serial2.print(float(CurrentTime / 1000)); Serial2.print(" lTrack received: "); Serial2.println(lTrack); 
      sendXBEEmsg(ACK_TRACK);
      break;

    default:
      numOfCycUnknown++;
      Serial2.print(float(CurrentTime / 1000)); Serial2.print(" Unknown character received: "); Serial2.println(processedMSG, HEX);
      break;
  }
}

boolean movemotor(boolean DIR, float pwmH, float pwmL){ //set motor velocity and direction
  
  if(pwmH > 255 || pwmL >255){  
    pwmH = 0;
    return 1;
    } //illigal values
  
  byte pwmHround = mround(pwmH);
  byte pwmLround = mround(pwmL);

  digitalWrite(dirPin,DIR); //maybe *255?
  analogWrite(pwmHPin, pwmHround);
  analogWrite(pwmLPin, pwmLround);
  return 0;
}

void IncrRevolution(){ //ISR function - measure revolutions
  
  Revolutions++;
  RunLength++;

}

void MeasureVelocityInPWM(unsigned int tDomain){ 
  
  long tDomainLong = (long) tDomain;

  measuredIn = (double) convertMagnetsToPWM(Revolutions, tDomainLong);
 
  Revolutions = 0;

  return; 

}

boolean checkTime(int sampleTime){ //returns 1 if more than  SAMPLE_TIME has past
   
   CurrentTime = millis();
   deltaT = CurrentTime - PreviousInterruptTime; //current time - previous time

   if(deltaT > sampleTime){
    PreviousInterruptTime = CurrentTime;
    return 1;
   }
 else{
   return 0;
    }
}

void stopMotor(){
  movemotor(DIR,0,MAX_PWM_VALUE);
}

boolean initSD(){ //initialize SD card
    if (!SD.begin(4)) {
        Serial2.println("ERROR - SD card initialization failed!");
        return 1;    // init failed
    }
    Serial2.println("SUCCESS - SD card initialized.");
    // check for index.htm file
    if (!SD.exists(WEBSITE_FILENAME)) {
        Serial2.println("ERROR - Can't find targuino.htm file!");
        return 1;  // can't find index file
    }
    Serial2.println("SUCCESS - Found htm file");
    return 0;
}

boolean sendFile(String Tfilename, EthernetClient cl){

  char cFilename[Tfilename.length()+1];
  Tfilename.toCharArray(cFilename, Tfilename.length()+1);

  TServerFile = SD.open(cFilename);        // open web page file
  if(TServerFile) {
    while(TServerFile.available() > 0){
       char c = TServerFile.read();
       cl.write(c); // send web page to client
      }
    TServerFile.close();
    return 0;
    }
  else{
    Serial2.print("ERROR - Can't open "); Serial2.println(cFilename);
    return 1;
  }
  }

void StrClear(char *str, char str_length){ // sets every element of str to 0 (clears array)
    for (int i = 0; i < str_length; i++){ str[i] = 0;}
}


unsigned int StrContains(char *str, char sfind[]){ // searches for the string sfind in the string str. returns the index of the last letter if string found, returns 0 if string not found
  char found = 0;
  char index = 0;
  char len;
  unsigned int iEnd = 0;

  len = strlen(str);
    
  if (strlen(sfind) > len){ 
    return 0; //any other value can be considered as an index value, so return 0/1 convention is not adequate here. 
  }

  while (index < len) {
      if (str[index] == sfind[found]){ 
        found++;
        iEnd = index;
        if (strlen(sfind) == found){ return iEnd;}
      }
      else{ found = 0;}
      index++;
  }
  return 0;
}

boolean sendHTTPResponse(char type, EthernetClient cl){
    cl.println("HTTP/1.1 200 OK");

  switch(type){
    case 'x':
      cl.println("Content-Type: text/xml");
      cl.println("Connection: keep-alive");
      break;
    case 'h':
      cl.println("Content-Type: text/html");
      cl.println("Connection: close");
      break;
    case 'c':
      cl.println("Content-Type: text/css");
      cl.println("Connection: close");
      break;
    case 'j':
      cl.println("Content-Type: text/html");
      cl.println("Connection: close");
      break;
    case 'g':
      cl.println("Content-Type: image/jpeg");
      cl.println("Connection: close");
      break;
    case 'i':
      cl.println("Content-Type: image/x-icon");
      cl.println("Connection: close");
      break;   
    default:
      return 1;
      break;
  }

  cl.println();
  return 0;
}

void coastMotor(){
  digitalWrite(pwmLPin,0);
  digitalWrite(pwmHPin,0);
}

void clrXBEEsendBuff(){
  msgToSend[1] = 0;
  msgToSend[2] = 0;
  msgToSend[3] = 0;
  msgToSend[4] = 0;
  msgToSend[5] = 0;
  msgToSend[6] = 0;
  msgToSend[7] = 0;
  msgToSend[8] = 0;

}

void clrXBEErecBuff(){
  recBuff[0] = 0;
  recBuff[1] = 0;
  recBuff[2] = 0;
  recBuff[3] = 0;
  recBuff[4] = 0;
  recBuff[5] = 0;
  recBuff[6] = 0;
  recBuff[7] = 0;

}

void sendXBEEmsg(byte buff){

  clrXBEEsendBuff();

  msgToSend[1] = buff;
  msgToSend[2] = buff;
  msgToSend[3] = buff;
  msgToSend[4] = MsgCounter;

  if(buff == LTR_VELOCITY_UPDATE){
    msgToSend[5] = (byte) (int) (velLTR * 10); //value range should be 0-35  
    //Serial2.print("vel = "); Serial2.print(msgToSend[5]);
  }
  else if(buff == LTR_DELAY_UPDATE){
    msgToSend[5] = (byte) (int) LTR_delay;   
   //Serial2.print("delay = "); Serial2.print(msgToSend[5]);
  }
  else if(buff == TRACK_LENGTH_UPDATE){
    msgToSend[5] = (byte) (int) (lTrack & 0xFF00);
    msgToSend[6] = (byte) (int) (lTrack & 0x00FF);   
    //Serial2.print("ltrack = "); Serial2.print(msgToSend[5]);
  }
  else if(buff == ACK_KA || buff == KEEP_ALIVE){
    msgToSend[5] = inMsgCount;
  }
  else if(buff == CLEAR_BUFFER){
    msgToSend[5] = msgIndDiff;
  }
  else{ msgToSend[5] = 0; }

  if(MsgCounter > 0xFE){ MsgCounter = 0; }
  
  Serial.write(msgToSend, 10);
  delay(40); //delay due to RO parameter on XBEE
  
  Serial2.print(float(CurrentTime / 1000)); Serial2.print(" Sent message number "); Serial2.print(MsgCounter); Serial2.print(": "); Serial2.print(buff, HEX); Serial2.print(" inMsgCount: "); Serial2.print(inMsgCount); Serial2.println(" ");

  previousTxMsg = buff;
  MsgCounter++;
}

byte procRecMsg(){
  
  //Serial2.print(" received message number "); Serial2.print(recBuff[3]);  Serial2.print(": "); Serial2.print(recBuff[0], HEX); Serial2.print(" "); Serial2.print(recBuff[1], HEX); Serial2.print(" "); Serial2.print(recBuff[2], HEX); Serial2.println("");
  
  //Serial2.print(recBuff[0] == recBuff[1]); Serial2.print(" "); Serial2.print(recBuff[0] == recBuff[2]); Serial2.print(" "); Serial2.print(recBuff[1] == recBuff[2]); 

  if(recBuff[0] == recBuff[1] || recBuff[0] == recBuff[2]){ return recBuff[0]; }
  else if(recBuff[1] == recBuff[2]){                        return recBuff[1]; }
  else{                                                     return 0xFF; }

}

void blinkLEDS(int tBetween, int times, boolean bothLEDS){
  int ntimes = 0;
  while(ntimes < times){
                  digitalWrite(LED1, LOW);
    if(bothLEDS){ digitalWrite(LED2, LOW); }  
    delay(tBetween);
                  digitalWrite(LED1, HIGH); 
    if(bothLEDS){ digitalWrite(LED2, HIGH); }
  }
}

boolean areVelocitiesLegal(){ //check wether the values for the velocities are correct
  if(velRTL > MAXIMUM_REQUESTED_VELOCITY || velLTR > MAXIMUM_REQUESTED_VELOCITY){ return 1;}
  else if(velRTL < 0.1 || velLTR < 0.1){ return 1;}
  else{ return 0;}
}

byte convertVelToMagnets(float inVel){

  float preciseCountedMagnets =  inVel * numOfMagnets * VMEASURE_SAMPLE_TIME * 100 / ( 2 * pi * ropeRadius * 1000 ); // for expected value calculation we can use the constant VMEASURE_SAMPLE_RATE
  
  return mround(preciseCountedMagnets);
}

byte convertMagnetsToPWM(byte inMagnets, long tDomainDiff){

  Serial2.print(CurrentTime); Serial2.print(" ##DEBUG rev: "); Serial2.print(Revolutions); Serial2.print(" Denum: "); Serial2.print(tDomainDiff * numOfMagnets * maximumMotorVelocity); Serial2.print(" deltaT: "); Serial2.println(deltaT);

  float PWMout = float(inMagnets) * 255 * 1000 / (tDomainDiff * numOfMagnets * maximumMotorVelocity); // for real-time calculation we need to use the real deltaT

  return mround(PWMout); 
}

byte convertVelToPWM(float vel){

  float precisePWMvalue = vel * 255 * 100 / ( maximumMotorVelocity * 2 * pi * ropeRadius );

  return mround(precisePWMvalue);
}

byte mround(float InValue){ //round a float number to the nearest integer by the first decimal.

  int integerPart = int(InValue);
  float remainPart = InValue - integerPart;

  if(remainPart > 0.5){ 
    return (byte) integerPart + 1 ;
  }
  else{
    return (byte) integerPart;
  }

}

struct parsedResult parseHTTPmsg(char *msg){
  
  parsedResult output;

  output.value = 99.99;
  output.fileToOpen = "";
  output.httpResponse = ' ';

  char temp[10] = "";


  //look for RTL velocity
  unsigned int ind = StrContains(msg, MSG_RTL_VEL);
  if(ind){
    output.msgType = UPDATE_VELOCITY_RTL;
    
    unsigned int andInd = StrContains(msg, "&");

    strncpy( temp, &msg[ind+1], andInd - ind + 1); //take only 2 first digits (ignore the last 0)
    output.value = atof(temp) / 10000;

    //Serial2.print("memcpy is:"); Serial2.print(temp); Serial2.print(" result is: "); Serial2.println(output.value);
    return output;
  }

  //look for LTR velocity
  ind = StrContains(msg, MSG_LTR_VEL);
  if(ind){
    output.msgType = UPDATE_VELOCITY_LTR;
    
    unsigned int andInd = StrContains(msg, "&");

    strncpy( temp, &msg[ind+1], andInd - ind + 1); //take only 2 first digits (ignore the last 0)
    output.value = atof(temp) / 10000;
    return output;
  }

  //look for BeginCalibration
  ind = StrContains(msg, MSG_CAL);
  if(ind){
    output.msgType = UPDATE_BEGIN_CALIBRATION;
    return output;
  }

  //look for BeginRun
  ind = StrContains(msg, MSG_RUN);
  if(ind){
    output.msgType = UPDATE_BEGIN_RUNNING;
    return output;
  }

  //look for StopSignal
  ind = StrContains(msg, MSG_STOP);
  if(ind){
    output.msgType = UPDATE_STOP;
    return output;
  }

 //look for status
  ind = StrContains(msg, MSG_STATUS);
  if(ind){
    output.msgType = UPDATE_STATUS;
    return output;
  }

   //look for targuino.CSS file
  ind = StrContains(msg, CSS_FILENAME);
  if(ind){
    output.msgType = OPEN_FILE;
    output.fileToOpen = CSS_FILENAME;
    output.httpResponse = 'c';
    return output;
  }

  //look for targuino.js file?
  ind = StrContains(msg, JAVASCRIPT_FILENAME);
  if(ind){
    output.msgType = OPEN_FILE;
    output.fileToOpen = JAVASCRIPT_FILENAME;
    output.httpResponse = 'j';
    return output;
  }
  
  //look for jpg file
  ind = StrContains(msg, JPG_FILENAME);
  if(ind){
    output.msgType = OPEN_FILE;
    output.fileToOpen = JPG_FILENAME;
    output.httpResponse = 'g';
    return output;
  }

  //look for htm file
  ind = StrContains(msg, WEBSITE_FILENAME);
  if(ind){
    output.msgType = OPEN_FILE;
    output.fileToOpen = WEBSITE_FILENAME;
    output.httpResponse = 'h';
    return output;
  }

  //look for png file
  ind = StrContains(msg, ICO_FILENAME);
  if(ind){
    output.msgType = OPEN_FILE;
    output.fileToOpen = ICO_FILENAME;
    output.httpResponse = 'i';
    return output;
  }

  //look for jquery file
  ind = StrContains(msg, JQUERY_FILENAME);
  if(ind){
    output.msgType = OPEN_FILE;
    output.fileToOpen = JQUERY_FILENAME;
    output.httpResponse = 'j';
    return output;
  }

  //look for uislider js file
  ind = StrContains(msg, JS_UISLIDER_FILENAME);
  if(ind){
    output.msgType = OPEN_FILE;
    output.fileToOpen = JS_UISLIDER_FILENAME;
    output.httpResponse = 'j';
    return output;
  }

  //look for uislider css file
  ind = StrContains(msg, CSS_UISLIDER_FILENAME);
  if(ind){
    output.msgType = OPEN_FILE;
    output.fileToOpen = CSS_UISLIDER_FILENAME;
    output.httpResponse = 'c';
    return output;
  }

  //look for RTL delay time update
  ind = StrContains(msg, MSG_RTL_DELAY);
  if(ind){
    output.msgType = UPDATE_DELAY_RTL;
    
    unsigned int andInd = StrContains(msg, "&");

    strncpy( temp, &msg[ind+1], andInd - ind);
    output.value = atoi(temp) / 1000; //same trick like with velocity: multiply by 1000 so it would be easy to be parsed
    return output;
  }

  //look for LTR delay time update
  ind = StrContains(msg, MSG_LTR_DELAY);
  if(ind){
    output.msgType = UPDATE_DELAY_LTR;
    
    unsigned int andInd = StrContains(msg, "&");

    strncpy( temp, &msg[ind+1], andInd - ind);
    output.value = atoi(temp) / 1000; //same trick like with velocity: multiply by 1000 so it would be easy to be parsed
    return output;
  }
}

void printXML(EthernetClient cl){
  cl.println("<?xml version = \"1.0\" ?>");
  cl.println("<Targuino>");
  cl.print("<RTL_Velocity>"); cl.print(velRTL); cl.println("</RTL_Velocity>");
  cl.print("<RTL_Delay>"); cl.print(RTL_delay); cl.println("</RTL_Delay>");
  cl.print("<LTR_Velocity>"); cl.print(velLTR); cl.println("</LTR_Velocity>");
  cl.print("<LTR_Delay>"); cl.print(LTR_delay); cl.println("</LTR_Delay>");
  cl.print("<SysMode>"); 
  if(sysMode == MS_IDLE){ cl.print("Idle"); }
  else if(sysMode == MS_CALIBRATION){ cl.print("Calibration"); }
  else if(sysMode == MS_RUNNING){ cl.print("Running"); } 
  cl.println("</SysMode>");
  cl.print("<Messages>"); cl.print(TarMsg); cl.println("</Messages>");
  cl.print("<XBEE_STATUS>"); cl.print(XBEEstatusMsg); cl.println("</XBEE_STATUS>");
  cl.print("<TrackLength>"); cl.print(lTrack * 2 * pi * ropeRadius / ( 100 * numOfMagnets)); cl.println("</TrackLength>");
  cl.print("</Targuino>");
}

void resetArduino(){
  digitalWrite(resetPin, LOW);
}

void setWaitForRespondMode(){
      FSM_State = WAIT_FOR_RESPONSE;
      PrevMsgSent = CurrentTime;
      numOfresends = 0;
      return;  
}

void cleanXBEE(){
  Serial2.print(float(CurrentTime / 1000)); Serial2.print(" forwarding incoming msgs "); Serial2.println(Serial.available());
  int i = 0;
  while(Serial.available() > 0 && i < recBuff[4]){
    tempByte = Serial.read();
    Serial2.print(tempByte,HEX); Serial2.print(" "); Serial2.println(i);
    i++;
  }
}
